# Fritzing sketch 아두이노 회로도 (saved by Fritzing 0.9.3b)
breadboards: 1

parts:
  부품1 = Arduino Uno (Rev3)
  J1 = Basic Servo
  DHT11_1 = DHT11 module
  J2 = Piezo Speaker
  Part1 = KY-019 5V Relay Module [package="Breakout board"]
  U1 = ESP8266 WiFi Module [part_number=ESP8266]
  LED1 = LED - 5mm [color="Red (633nm)" package="5 mm [THT]"]
  R1 = Resistor [tolerance=±5% resistance=330 package=THT]
  Part2 = KY-023 Dual Axis Joystick Module [package="Breakout board"]

nets:
  N1: 부품1.A0, Part2.VRx
  N2: 부품1.A1, Part2.VRy
  N3: 부품1.D8, Part2.SW
  N4: 부품1.D9_PWM, U1.RXD
  N5: 부품1.D10_PWM/SS, U1.TXD
  N6: 부품1.D12/MISO, Part1.S
  N7: 부품1.D7, DHT11_1.DATA
  3V3: 부품1.3V3, U1.VCC, U1.CH_PD
  VCC: 부품1.5V, J1.vcc, DHT11_1.VCC, Part1.+, LED1.anode, Part2.+5V
  GND: 부품1.GND, J1.gnd, DHT11_1.GND, J2.pin1, Part1.-, U1.GND, R1.Pin_0, Part2.GND
  N8: LED1.cathode, R1.Pin_1

custom parts:
  DHT11 module: DHT11 black pcb module
  KY-019 5V Relay Module: KY-019 5V Relay module, used to control AC circuits.
  ESP8266 WiFi Module: Generic WiFi Module based on the ESP8266 with onboard PCB antenna and UART communications
